# Fritzing sketch Light_Theremin_REV_A (saved by Fritzing 0.9.3b)
circuit board: 3.41773cm x 3.15181cm
breadboards: 1

parts:
  555 = 555 Timer [package="DIP8 [THT]"]
  R1 = Resistor [tolerance=±5% resistance=10k package=THT]
  LDR = Photocell (LDR) [package=THT]
  R3 = Resistor [tolerance=±5% resistance=1M package=THT]
  Speaker = Piezo Speaker
  C1 = Electrolytic Capacitor [capacitance=100µF package="100 mil [THT, electrolytic]"]
  C2 = Ceramic Capacitor [capacitance=22µF package="100 mil [THT, multilayer]"]
  C3 = Ceramic Capacitor [capacitance=22µF package="100 mil [THT, multilayer]"]

nets:
  N1: 555.Ground, R3.Pin_1, Speaker.pin1, C2.1, C3.1
  N2: 555.Trigger, 555.Threshold, LDR.pin_0, R3.Pin_0, C2.0, C3.0
  N3: 555.Output, C1.+
  N4: 555.Reset, 555.Vcc_Supply_Voltage, R1.Pin_1
  N5: 555.Discharge, R1.Pin_0, LDR.pin_1
  N6: Speaker.pin2, C1.-

notes:
  Bat -
  Bat +
  Light Theremin
  -
  +
  6V
  REV A
